# Fritzing sketch Circuit Sketch1 (saved by Fritzing 0.9.3b)
breadboards: 1

parts:
  Part5 = Arduino Uno (Rev3) - ICSP
  J8 = Basic Servo
  J9 = Basic Servo
  J10 = Basic Servo
  J11 = Basic Servo
  J12 = Basic Servo
  J13 = Basic Servo
  BAT2 = BC9VPC [package=bc9vpc]

nets:
  N1: Part5.D6_PWM, J11.pulse, J12.pulse, J13.pulse
  N2: Part5.D7, J8.pulse, J9.pulse, J10.pulse
  GND: Part5.GND, J8.gnd, J9.gnd, J10.gnd, J11.gnd, J12.gnd, J13.gnd, BAT2.V-
  VCC: J9.vcc, J10.vcc, J11.vcc, J12.vcc, J13.vcc
